# Fritzing sketch wifi (saved by Fritzing 0.9.2b)
breadboards: 1

parts:
  Εξάρτημα1 = Arduino Uno (Rev3)
  U2 = Voltage Regulator -- 3.3 V -- LM1117
  C1 = Electrolytic Capacitor [capacitance=1µF package="100 mil [THT, electrolytic]"]
  D1 = Rectifier Diode [part_number=1N4001 package="300 mil [THT]"]
  U1 = ESP8266 WiFi Module [part_number=ESP8266]

nets:
  N1: Εξάρτημα1.D8, D1.cathode
  N2: Εξάρτημα1.D9_PWM, U1.TXD
  N3: Εξάρτημα1.5V, U2.IN, C1.+
  GND: Εξάρτημα1.GND, U2.GND, C1.-, U1.GND
  N4: U2.OUT, U1.VCC, U1.GPIO_2, U1.CH_PD
  N5: D1.anode, U1.RXD, U1.GPIO_0

custom parts:
  Voltage Regulator -- 3.3 V -- LM1117: LM1117-3.3 Voltage regulator, 3.3 V output. Note that the pinout order is not the same as LM7805 or LM7833.
  ESP8266 WiFi Module: Generic WiFi Module based on the ESP8266 with onboard PCB antenna and UART communications
